# Fritzing sketch buzzer+ultrassonico+microservo (saved by Fritzing 0.9.3b)
breadboards: 1

parts:
  HC-SR04_Sensor_1 = HC-SR04 Ultrasonic Distance Sensor
  J1 = Piezo Speaker
  U1 = NodeMCU V1.0
  J2 = Basic Servo

nets:
  VCC: HC-SR04_Sensor_1.VCC, J2.vcc
  N1: HC-SR04_Sensor_1.TRIG, U1.D2
  N2: HC-SR04_Sensor_1.ECHO, U1.D3
  GND: HC-SR04_Sensor_1.GND, J1.pin1, U1.GND, J2.gnd
  N3: J1.pin2, U1.D4

custom parts:
  NodeMCU V1.0: ESP8266 based NodeMCU
